// Logisim project 24125102_01.circ as structural Verilog: 3 circuits, main circuit main
module main (
  input  [3:0] in_1,
  input  [3:0] in_2,
  input  in_3,
  output [3:0] out_4,
  output out_5
);

  wire full_adder_1_hi, full_adder_2_hi, full_adder_3_hi;

  full_adder full_adder_1 (.A(in_1[0]), .B(in_2[0]), .C(in_3), .lo(out_4[0]), .hi(full_adder_1_hi));
  full_adder full_adder_2 (.A(in_1[1]), .B(in_2[1]), .C(full_adder_1_hi), .lo(out_4[1]), .hi(full_adder_2_hi));
  full_adder full_adder_3 (.A(in_1[2]), .B(in_2[2]), .C(full_adder_2_hi), .lo(out_4[2]), .hi(full_adder_3_hi));
  full_adder full_adder_4 (.A(in_1[3]), .B(in_2[3]), .C(full_adder_3_hi), .lo(out_4[3]), .hi(out_5));
endmodule

module full_adder (
  input  A,
  input  B,
  input  C,
  output lo,
  output hi
);

  wire half_adder_1_hi, half_adder_1_lo, half_adder_2_hi;

  half_adder half_adder_1 (.A(A), .B(B), .lo(half_adder_1_lo), .hi(half_adder_1_hi));
  half_adder half_adder_2 (.A(half_adder_1_lo), .B(C), .lo(lo), .hi(half_adder_2_hi));
  or or_1 (hi, half_adder_2_hi, half_adder_1_hi);
endmodule

module half_adder (
  input  A,
  input  B,
  output lo,
  output hi
);

  xor xor_1 (lo, A, B);
  and and_1 (hi, A, B);
endmodule
