// Logisim project 24125102_02.circ as structural Verilog: 3 circuits, main circuit main
module main (
  input  [7:0] in_1,
  input  [7:0] in_2,
  input  in_3,
  output [7:0] out_4,
  output out_5
);

  wire full_adder_1_hi, full_adder_2_hi, full_adder_3_hi, full_adder_4_hi, full_adder_5_hi, full_adder_6_hi,
       full_adder_7_hi, full_adder_8_hi, not_2_out;
  wire [7:0] not_1_out;

  assign not_1_out = ~in_2;  // NOT_Gate not_1, 8 bits wide
  not not_2 (not_2_out, in_3);
  not not_3 (out_5, full_adder_8_hi);
  full_adder full_adder_1 (.A(in_1[0]), .B(not_1_out[0]), .C(not_2_out), .lo(out_4[0]), .hi(full_adder_1_hi));
  full_adder full_adder_2 (.A(in_1[1]), .B(not_1_out[1]), .C(full_adder_1_hi), .lo(out_4[1]), .hi(full_adder_2_hi));
  full_adder full_adder_3 (.A(in_1[2]), .B(not_1_out[2]), .C(full_adder_2_hi), .lo(out_4[2]), .hi(full_adder_3_hi));
  full_adder full_adder_4 (.A(in_1[3]), .B(not_1_out[3]), .C(full_adder_3_hi), .lo(out_4[3]), .hi(full_adder_4_hi));
  full_adder full_adder_5 (.A(in_1[4]), .B(not_1_out[4]), .C(full_adder_4_hi), .lo(out_4[4]), .hi(full_adder_5_hi));
  full_adder full_adder_6 (.A(in_1[5]), .B(not_1_out[5]), .C(full_adder_5_hi), .lo(out_4[5]), .hi(full_adder_6_hi));
  full_adder full_adder_7 (.A(in_1[6]), .B(not_1_out[6]), .C(full_adder_6_hi), .lo(out_4[6]), .hi(full_adder_7_hi));
  full_adder full_adder_8 (.A(in_1[7]), .B(not_1_out[7]), .C(full_adder_7_hi), .lo(out_4[7]), .hi(full_adder_8_hi));
endmodule

module half_adder (
  input  A,
  input  B,
  output lo,
  output hi
);

  xor xor_1 (lo, A, B);
  and and_1 (hi, A, B);
endmodule

module full_adder (
  input  A,
  input  B,
  input  C,
  output lo,
  output hi
);

  wire half_adder_1_hi, half_adder_1_lo, half_adder_2_hi;

  half_adder half_adder_1 (.A(A), .B(B), .lo(half_adder_1_lo), .hi(half_adder_1_hi));
  half_adder half_adder_2 (.A(half_adder_1_lo), .B(C), .lo(lo), .hi(half_adder_2_hi));
  or or_1 (hi, half_adder_2_hi, half_adder_1_hi);
endmodule
