// Logisim project 24125102_03.circ as structural Verilog: 3 circuits, main circuit main
module main (
  input  [3:0] A,
  input  [3:0] B,
  input  C,
  input  S,
  output [3:0] out_5,
  output out_6
);

  wire full_adder_1_hi, full_adder_2_hi, full_adder_3_hi, full_adder_4_hi, full_adder_5_hi, full_adder_6_hi,
       full_adder_7_hi, full_adder_8_hi, not_2_out, not_3_out;
  wire [3:0] full_adder_1_lo, full_adder_2_lo, not_1_out;

  assign not_1_out = ~B;  // NOT_Gate not_1, 4 bits wide
  Multiplexer #(.width(4)) multiplexer_1 (.in0(full_adder_1_lo), .in1(full_adder_2_lo), .out(out_5), .sel(S));
  Multiplexer multiplexer_2 (.in0(full_adder_7_hi), .in1(not_3_out), .out(out_6), .sel(S));
  not not_2 (not_2_out, C);
  full_adder full_adder_1 (.A(A[0]), .B(B[0]), .C(C), .lo(full_adder_1_lo[0]), .hi(full_adder_1_hi));
  full_adder full_adder_2 (.A(A[0]), .B(not_1_out[0]), .C(not_2_out), .lo(full_adder_2_lo[0]), .hi(full_adder_2_hi));
  full_adder full_adder_3 (.A(A[1]), .B(B[1]), .C(full_adder_1_hi), .lo(full_adder_1_lo[1]), .hi(full_adder_3_hi));
  full_adder full_adder_4 (
    .A(A[1]), .B(not_1_out[1]), .C(full_adder_2_hi), .lo(full_adder_2_lo[1]), .hi(full_adder_4_hi));
  full_adder full_adder_5 (.A(A[2]), .B(B[2]), .C(full_adder_3_hi), .lo(full_adder_1_lo[2]), .hi(full_adder_5_hi));
  full_adder full_adder_6 (
    .A(A[2]), .B(not_1_out[2]), .C(full_adder_4_hi), .lo(full_adder_2_lo[2]), .hi(full_adder_6_hi));
  full_adder full_adder_7 (.A(A[3]), .B(B[3]), .C(full_adder_5_hi), .lo(full_adder_1_lo[3]), .hi(full_adder_7_hi));
  full_adder full_adder_8 (
    .A(A[3]), .B(not_1_out[3]), .C(full_adder_6_hi), .lo(full_adder_2_lo[3]), .hi(full_adder_8_hi));
  not not_3 (not_3_out, full_adder_8_hi);
endmodule

module half_adder (
  input  A,
  input  B,
  output lo,
  output hi
);

  xor xor_1 (lo, A, B);
  and and_1 (hi, A, B);
endmodule

module full_adder (
  input  A,
  input  B,
  input  C,
  output lo,
  output hi
);

  wire half_adder_1_hi, half_adder_1_lo, half_adder_2_hi;

  half_adder half_adder_1 (.A(A), .B(B), .lo(half_adder_1_lo), .hi(half_adder_1_hi));
  half_adder half_adder_2 (.A(half_adder_1_lo), .B(C), .lo(lo), .hi(half_adder_2_hi));
  or or_1 (hi, half_adder_2_hi, half_adder_1_hi);
endmodule
