// Logisim project 24125102_04.circ as structural Verilog: 2 circuits, main circuit main
module main (
  input  [3:0] in_1,
  input  [3:0] in_2,
  input  in_3,
  output [3:0] out_4,
  output out_5
);

  wire [2:0] undriven;
  wire [8:1] plarom_1_p1;

  partial_adder partial_adder_1 (
    .A(in_1[0]), .B(in_2[0]), .C(in_3), .lo(out_4[0]), .P(plarom_1_p1[4]), .G(plarom_1_p1[8]));
  partial_adder partial_adder_2 (
    .A(in_1[1]), .B(in_2[1]), .C(undriven[0]), .lo(out_4[1]), .P(plarom_1_p1[3]), .G(plarom_1_p1[7]));
  // PlaRom #(.Contents("2 0*12 2 0*3 2 0 2 0*7 2 0*4 2 0*7 2 2 0 0 2 0 0 2 0*7 2 0*4 2 0 0 2 0*4 2 2 0*6 2*3 0 2 0*3 2 0*7 2 0*4 2 0 0 2 0*4 2 2 0 2 0*4 2*3 0*5 2*5 0*3 1 0*3 1 0 0 1 0*3 1 0*3 1 0 0 1 0*3 1 0*3 1 0*3 1 0 0 1 0*3 1 0*3 1 0*3 1 0*3 1 0*3"), .\and (14)) plarom_1: pin names not known; wires that end beside it: {plarom_1_p1, in_3}
  partial_adder partial_adder_3 (
    .A(in_1[2]), .B(in_2[2]), .C(undriven[1]), .lo(out_4[2]), .P(plarom_1_p1[2]), .G(plarom_1_p1[6]));
  partial_adder partial_adder_4 (
    .A(in_1[3]), .B(in_2[3]), .C(undriven[2]), .lo(out_4[3]), .P(plarom_1_p1[1]), .G(plarom_1_p1[5]));
endmodule

module partial_adder (
  input  A,
  input  B,
  input  C,
  output lo,
  output P,
  output G
);

  xor xor_1 (lo, A, B, C);
  or or_1 (P, A, B);
  and and_1 (G, A, B);
endmodule
