// Logisim project 24125102_05.circ as structural Verilog: 7 circuits, main circuit main
module main (
  input  [3:0] in_1,
  input  [3:0] in_2,
  input  [3:0] in_3,
  input  [3:0] in_4,
  input  in_5,
  output [3:0] out_6,
  output [3:0] out_7,
  output out_8
);

  wire bcd_full_adder_1_hi;

  BCD_full_adder bcd_full_adder_1 (.A(in_2), .B(in_4), .C(in_5), .S(out_7), .hi(bcd_full_adder_1_hi));
  BCD_full_adder bcd_full_adder_2 (.A(in_1), .B(in_3), .C(bcd_full_adder_1_hi), .S(out_6), .hi(out_8));
endmodule

module half_adder (
  input  A,
  input  B,
  output lo,
  output hi
);

  xor xor_1 (lo, A, B);
  and and_1 (hi, A, B);
endmodule

module full_adder (
  input  A,
  input  B,
  input  C,
  output lo,
  output hi
);

  wire half_adder_1_hi, half_adder_1_lo, half_adder_2_hi, half_adder_3_hi;

  half_adder half_adder_1 (.A(A), .B(B), .lo(half_adder_1_lo), .hi(half_adder_1_hi));
  half_adder half_adder_2 (.A(half_adder_1_lo), .B(C), .lo(lo), .hi(half_adder_2_hi));
  half_adder half_adder_3 (.A(half_adder_2_hi), .B(half_adder_1_hi), .lo(hi), .hi(half_adder_3_hi));
  // NoConnect on half_adder_3_hi
endmodule

module swag_adder (
  input  [3:0] A,
  input  [3:0] B,
  input  C,
  output [3:0] S,
  output hi
);

  wire full_adder_1_hi, full_adder_2_hi, full_adder_3_hi;

  full_adder full_adder_1 (.A(A[0]), .B(B[0]), .C(C), .lo(S[0]), .hi(full_adder_1_hi));
  full_adder full_adder_2 (.A(A[1]), .B(B[1]), .C(full_adder_1_hi), .lo(S[1]), .hi(full_adder_2_hi));
  full_adder full_adder_3 (.A(A[2]), .B(B[2]), .C(full_adder_2_hi), .lo(S[2]), .hi(full_adder_3_hi));
  full_adder full_adder_4 (.A(A[3]), .B(B[3]), .C(full_adder_3_hi), .lo(S[3]), .hi(hi));
endmodule

module correctable (
  input  [3:0] D,
  output f
);

  wire and_1_out, and_2_out;

  // NoConnect on D[0]
  and and_1 (and_1_out, D[1], D[3]);
  and and_2 (and_2_out, D[2], D[3]);
  or or_1 (f, and_1_out, and_2_out);
endmodule

module BCD_half_adder (
  input  [3:0] A,
  input  [3:0] B,
  output [3:0] S,
  output C
);

  wire correctable_1_f, swag_adder_1_hi, swag_adder_2_hi;
  wire [3:0] swag_adder_1_s;

  correctable correctable_1 (.D(swag_adder_1_s), .f(correctable_1_f));
  swag_adder swag_adder_1 (.A(A), .B(B), .S(swag_adder_1_s), .hi(swag_adder_1_hi));  // open: C
  or or_1 (C, correctable_1_f, swag_adder_1_hi);
  swag_adder swag_adder_2 (.A(swag_adder_1_s), .B({1'b0, {2{C}}, 1'b0}), .S(S), .hi(swag_adder_2_hi));  // open: C
  // NoConnect on swag_adder_2_hi
endmodule

module BCD_full_adder (
  input  [3:0] A,
  input  [3:0] B,
  input  C,
  output [3:0] S,
  output hi
);

  wire bcd_half_adder_1_c, bcd_half_adder_2_c;
  wire [3:0] bcd_half_adder_1_s;

  BCD_half_adder bcd_half_adder_1 (.A(A), .B(B), .S(bcd_half_adder_1_s), .C(bcd_half_adder_1_c));
  BCD_half_adder bcd_half_adder_2 (.A(bcd_half_adder_1_s), .B({3'b000, C}), .S(S), .C(bcd_half_adder_2_c));
  or or_1 (hi, bcd_half_adder_1_c, bcd_half_adder_2_c);
endmodule
