// Logisim project 24125102_06.circ as structural Verilog: 1 circuit, main circuit main
module main (
  input  [7:0] in_1,
  input  [7:0] in_2,
  input  in_3,
  output [7:0] out_4,
  output out_5
);

  wire n74181_1_p14, n74182_1_pin1, n74182_1_pin2, n74182_1_pin4, n74182_1_pin11, n74182_1_pin12, not_1_out;

  not not_1 (not_1_out, in_3);
  not not_2 (out_5, n74182_1_pin11);
  // _74181 #(.ShowInternalStructure("true")) 74181_1: pin names not known; wires that end beside it: in_2[0], in_1[1], in_1[0], in_2[1], 1'b1, in_1[2], 1'b0, in_2[2], 1'b0, in_1[3], 1'b1, in_2[3], not_1_out, n74181_1_p14, 1'b0, out_4[0]
  _74182 #(.ShowInternalStructure("true")) u_74182_1 (
    .pin1(n74182_1_pin1), .pin2(n74182_1_pin2), .pin3(n74181_1_p14), .pin4(n74182_1_pin4), .pin13(not_1_out),
    .pin12(n74182_1_pin12), .pin11(n74182_1_pin11));  // open: pin5, pin6, pin7, pin15, pin14, pin10, pin9
  // _74181 #(.ShowInternalStructure("true")) 74181_2: pin names not known; wires that end beside it: n74182_1_pin4, out_4[1], out_4[2], out_4[3], in_2[4], in_1[5], in_1[4], in_2[5], 1'b1, in_1[6], 1'b0, in_2[6], 1'b0, in_1[7], 1'b1, in_2[7], n74182_1_pin12, n74182_1_pin1, 1'b0, out_4[4], n74182_1_pin2, out_4[5], out_4[6], out_4[7]
endmodule
