// Logisim project lab_mips.circ as structural Verilog: 9 circuits, main circuit main
module main (
);

  wire button_1_out, CLK, keyboard_1_avail, MHalf, MRead, MSigned, MWord, MWrite, northbridge_1_ioclk,
       northbridge_1_ioread, northbridge_1_iowrite, northbridge_1_memclk, northbridge_1_memstr,
       northbridge_1_memstr0, northbridge_1_memstr1, northbridge_1_memstr2, northbridge_1_memstr3, RS,
       southbridge_1_kbdclk, southbridge_1_kbdread, southbridge_1_lcdclk, southbridge_1_lcdwrite;
  wire [1:0] CS, JS;
  wire [2:0] B0_out;
  wire [4:0] decode_1_cond, DS, Op, SH, XS, YS;
  wire [6:0] keyboard_1_data, southbridge_1_lcddata;
  wire [7:0] Program_Memory_p1, Program_Memory_p2, Program_Memory_p3, Program_Memory_p4, ram_1_p12,
       ram_1_p13, ram_1_p14, ram_1_p15, southbridge_1_lowerleddata, southbridge_1_lowerleddata_2,
       southbridge_1_lowerleddata_3, southbridge_1_lowerleddata_4, southbridge_1_sevendata,
       southbridge_1_upperleddata, southbridge_1_upperleddata_2, southbridge_1_upperleddata_3,
       southbridge_1_upperleddata_4;
  wire [9:0] southbridge_1_leddata, SWITCHES_p10;
  wire [11:0] northbridge_1_atoio, northbridge_1_atomem, PC_q;
  wire [31:0] alu_1_r, branchcalc_1_broffset, decode_1_pcabsolute, multiplexer_1_out, multiplexer_2_out,
       multiplexer_3_out, northbridge_1_dout, northbridge_1_dtoio, northbridge_1_dtomem, PCplus4, plus_1_v,
       Register_File_x, Register_File_y, SI, southbridge_1_dout, ZI;
  wire [31:12] PC_q_2;

  Register #(.width(32)) PC (.D(multiplexer_1_out), .Q({PC_q_2, PC_q}), .clk(CLK), .clr(button_1_out));  // open: en
  Button button_1 (.out(button_1_out));
  Multiplexer #(.select(2), .width(32)) multiplexer_1 (
    .in0(PCplus4), .in1(plus_1_v), .in2(Register_File_x), .in3(decode_1_pcabsolute), .out(multiplexer_1_out),
    .sel(JS));
  // ROM #(.addrWidth(12), .line("quad")) Program_Memory: pin names not known; wires that end beside it: Program_Memory_p1, Program_Memory_p2, Program_Memory_p3, Program_Memory_p4
  plus plus_1 (.A({PC_q_2, PC_q}), .B(branchcalc_1_broffset), .V(plus_1_v));
  plusfour plusfour_1 (.A({PC_q_2, PC_q}), .V(PCplus4));
  Clock u_CLK (.out(CLK));
  branchcalc branchcalc_1 (
    .Y(Register_File_y), .cond(decode_1_cond), .SImm(SI), .X(Register_File_x),
    .BrOffset(branchcalc_1_broffset));
  regfile Register_File (
    .XS(XS), .YS(YS), .clk(CLK), .DS(DS), .D(multiplexer_3_out), .X(Register_File_x), .Y(Register_File_y));
  decode decode_1 (
    .Instr({Program_Memory_p1, Program_Memory_p2, Program_Memory_p3, Program_Memory_p4}), .YS(YS), .JS(JS),
    .cond(decode_1_cond), .CS(CS), .AluOp(Op), .RS(RS), .ZI(ZI), .SI(SI), .PCAbsolute(decode_1_pcabsolute),
    .MWrite(MWrite), .MRead(MRead), .MHalf(MHalf), .MWord(MWord), .MSigned(MSigned), .out_12(SH), .DS(DS),
    .XS(XS));
  Multiplexer #(.select(2), .width(32)) multiplexer_2 (
    .in0(Register_File_y), .in1(ZI), .in2(SI), .in3(PCplus4), .out(multiplexer_2_out), .sel(CS));
  ALU alu_1 (.Y(multiplexer_2_out), .X(Register_File_x), .CLK(CLK), .Op(Op), .sh(SH), .R(alu_1_r));
  northbridge northbridge_1 (
    .word(MWord), .\signed (MSigned), .half(MHalf), .A(alu_1_r), .write(MWrite), .read(MRead), .clk(CLK),
    .Din(Register_File_y), .DfromIO(southbridge_1_dout),
    .DfromMem({ram_1_p12, ram_1_p13, ram_1_p14, ram_1_p15}), .IORead(northbridge_1_ioread),
    .DtoIO(northbridge_1_dtoio), .IOWrite(northbridge_1_iowrite), .AtoIO(northbridge_1_atoio),
    .Dout(northbridge_1_dout), .IOClk(northbridge_1_ioclk), .DtoMem(northbridge_1_dtomem),
    .AtoMem(northbridge_1_atomem), .MemClk(northbridge_1_memclk), .MemStr(northbridge_1_memstr),
    .MemStr3(northbridge_1_memstr3), .MemStr2(northbridge_1_memstr2), .MemStr1(northbridge_1_memstr1),
    .MemStr0(northbridge_1_memstr0));
  southbridge southbridge_1 (
    .A(northbridge_1_atoio), .Din(northbridge_1_dtoio), .read(northbridge_1_ioread),
    .write(northbridge_1_iowrite), .BtnData(SWITCHES_p10), .clk(northbridge_1_ioclk), .SwData(B0_out),
    .KbdData(keyboard_1_data), .KbdReady(keyboard_1_avail), .Dout(southbridge_1_dout),
    .UpperLedData({southbridge_1_upperleddata_4, southbridge_1_upperleddata_3, southbridge_1_upperleddata_2, southbridge_1_upperleddata}),
    .LowerLedData({southbridge_1_lowerleddata_4, southbridge_1_lowerleddata_3, southbridge_1_lowerleddata_2, southbridge_1_lowerleddata}),
    .SevenData(southbridge_1_sevendata), .LcdData(southbridge_1_lcddata), .LcdWrite(southbridge_1_lcdwrite),
    .LcdClk(southbridge_1_lcdclk), .KbdRead(southbridge_1_kbdread), .KbdClk(southbridge_1_kbdclk),
    .LedData(southbridge_1_leddata));
  // RAM #(.addrWidth(12), .enables("line"), .line("quad"), .\type ("nonvolatile")) ram_1: pin names not known; wires that end beside it: northbridge_1_atomem, northbridge_1_memstr, northbridge_1_memstr0, northbridge_1_memstr1, northbridge_1_memstr2, northbridge_1_memstr3, northbridge_1_memclk, northbridge_1_dtomem[31:24], northbridge_1_dtomem[23:16], northbridge_1_dtomem[15:8], northbridge_1_dtomem[7:0], ram_1_p12, ram_1_p13, ram_1_p14, ram_1_p15
  TTY tty_1 (.data(southbridge_1_lcddata), .clk(southbridge_1_lcdclk), .we(southbridge_1_lcdwrite));  // open: clr
  Keyboard keyboard_1 (
    .clk(southbridge_1_kbdclk), .re(southbridge_1_kbdread), .avail(keyboard_1_avail), .data(keyboard_1_data));  // open: clr
  DotMatrix #(.inputtype("row"), .matrixcols(8), .matrixrows(8)) dotmatrix_1 (
    .row0(southbridge_1_upperleddata), .row1(southbridge_1_upperleddata_2),
    .row2(southbridge_1_upperleddata_3), .row3(southbridge_1_upperleddata_4),
    .row4(southbridge_1_lowerleddata), .row5(southbridge_1_lowerleddata_2),
    .row6(southbridge_1_lowerleddata_3), .row7(southbridge_1_lowerleddata_4));
  Multiplexer #(.width(32)) multiplexer_3 (.in0(alu_1_r), .in1(northbridge_1_dout), .out(multiplexer_3_out), .sel(RS));
  LED L9 (.in(southbridge_1_leddata[9]));
  LED L8 (.in(southbridge_1_leddata[8]));
  LED L7 (.in(southbridge_1_leddata[7]));
  LED L6 (.in(southbridge_1_leddata[6]));
  // Binary_to_BCD_converter #(.binvalue(8)) binary_to_bcd_converter_1: pin names not known; wires that end beside it: southbridge_1_sevendata
  LED L5 (.in(southbridge_1_leddata[5]));
  LED L4 (.in(southbridge_1_leddata[4]));
  LED L3 (.in(southbridge_1_leddata[3]));
  LED L2 (.in(southbridge_1_leddata[2]));
  Button B2 (.out(B0_out[2]));
  // DipSwitch #(.number(10)) SWITCHES: pin names not known; wires that end beside it: SWITCHES_p10[9], SWITCHES_p10[8], SWITCHES_p10[7], SWITCHES_p10[6], SWITCHES_p10[5], SWITCHES_p10[4], SWITCHES_p10[3], SWITCHES_p10[2], SWITCHES_p10[1], SWITCHES_p10[0]
  _7_Segment_Display u_7_segment_display_1 ();  // open: g, f, a, b, e, d, c, dp
  _7_Segment_Display u_7_segment_display_2 ();  // open: g, f, a, b, e, d, c, dp
  // BCD_to_7_Segment_decoder bcd_to_7_segment_decoder_1: pin names not known
  // BCD_to_7_Segment_decoder bcd_to_7_segment_decoder_2: pin names not known
  LED L1 (.in(southbridge_1_leddata[1]));
  LED L0 (.in(southbridge_1_leddata[0]));
  Button B1 (.out(B0_out[1]));
  Button B0 (.out(B0_out[0]));

  // Notes on the sheet:
  //   contents of Program_Memory (hex, n*v repeats v):
  //   3c 1 80 0 34 22 0 18 ac 40 0 0 ac 40 0 4 24 5 0 0 24 b 0 0 3c 1 80 0 34 22 0 10 8c 43 0 0 0 3 1a c2
  //   30 63 0 1 10 60 ff f9 15 60 ff f9 14 60 0 1 8 0 0 6 24 a5 0 1 24 4 0 4 0 a4 0 1a 0 0 28 12 3c 1 80 0
  //   34 22 0 18 24 4 0 8 0 a4 0 18 0 0 28 12 8c a6 0 0 ac 46 0 0 8c a6 0 4 ac 46 0 4 0 a4 0 1a 0 0 28 10
  //   24 b 0 1 8 0 0 6
endmodule

module decode (
  input  [31:0] Instr,
  output [1:0] JS,
  output [4:0] cond,
  output [1:0] CS,
  output [4:0] AluOp,
  output MWrite,
  output MRead,
  output MHalf,
  output MWord,
  output RS,
  output MSigned,
  output [4:0] out_12,
  output [31:0] ZI,
  output [4:0] DS,
  output [4:0] XS,
  output [4:0] YS,
  output [31:0] SI,
  output [31:0] PCAbsolute
);

  wire [3:0] regimm_out, regsel_out;
  wire [23:0] pla_1_out;
  wire [24:0] arith_out;

  PLA #(.in_width(32), .out_width(24), .\table ("000000xxxxxxxxxxxxxxxxxxxxxxxxxx 000000000000000000000001 # ARITH\n000001xxxxxxxxxxxxxxxxxxxxxxxxxx 000000000000000000000010 # REGIMM\n000010xxxxxxxxxxxxxxxxxxxxxxxxxx 000000000000000000000100 # J\n000011xxxxxxxxxxxxxxxxxxxxxxxxxx 000000000000000000001000 # JAL\n000100xxxxxxxxxxxxxxxxxxxxxxxxxx 000000000000000000010000 # BEQ\n000101xxxxxxxxxxxxxxxxxxxxxxxxxx 000000000000000000100000 # BNE\n000110xxxxxxxxxxxxxxxxxxxxxxxxxx 000000000000000001000000 # BLEZ\n000111xxxxxxxxxxxxxxxxxxxxxxxxxx 000000000000000010000000 # BGTZ\n001000xxxxxxxxxxxxxxxxxxxxxxxxxx 000000000000000100000000 # ADDI\n001001xxxxxxxxxxxxxxxxxxxxxxxxxx 000000000000001000000000 # ADDIU\n001010xxxxxxxxxxxxxxxxxxxxxxxxxx 000000000000010000000000 # SLTI\n001011xxxxxxxxxxxxxxxxxxxxxxxxxx 000000000000100000000000 # SLTIU\n001100xxxxxxxxxxxxxxxxxxxxxxxxxx 000000000001000000000000 # ANDI\n001101xxxxxxxxxxxxxxxxxxxxxxxxxx 000000000010000000000000 # ORI\n001110xxxxxxxxxxxxxxxxxxxxxxxxxx 000000000100000000000000 # XORI\n001111xxxxxxxxxxxxxxxxxxxxxxxxxx 000000001000000000000000 # LUI\n100000xxxxxxxxxxxxxxxxxxxxxxxxxx 000000010000000000000000 # LB\n100001xxxxxxxxxxxxxxxxxxxxxxxxxx 000000100000000000000000 # LH\n100011xxxxxxxxxxxxxxxxxxxxxxxxxx 000001000000000000000000 # LW\n100100xxxxxxxxxxxxxxxxxxxxxxxxxx 000010000000000000000000 # LBU\n100101xxxxxxxxxxxxxxxxxxxxxxxxxx 000100000000000000000000 # LHU\n101000xxxxxxxxxxxxxxxxxxxxxxxxxx 001000000000000000000000 # SB\n101001xxxxxxxxxxxxxxxxxxxxxxxxxx 010000000000000000000000 # SH\n101011xxxxxxxxxxxxxxxxxxxxxxxxxx 100000000000000000000000 # SW\nxxxxxxxxxxxxxxxxxxxxxxxxxxxxxxxx 000000000000000000000000 # UNIMPL\n010000xxxxxxxxxxxxxxxxxxxxxxxxxx 000000000000000000000000 # COP0\n010001xxxxxxxxxxxxxxxxxxxxxxxxxx 000000000000000000000000 # COP1\n010010xxxxxxxxxxxxxxxxxxxxxxxxxx 000000000000000000000000 # COP2\n010011xxxxxxxxxxxxxxxxxxxxxxxxxx 000000000000000000000000 # COP3\n100010xxxxxxxxxxxxxxxxxxxxxxxxxx 000000000000000000000000 # LWL\n100110xxxxxxxxxxxxxxxxxxxxxxxxxx 000000000000000000000000 # LWR\n101010xxxxxxxxxxxxxxxxxxxxxxxxxx 000000000000000000000000 # SWL\n101110xxxxxxxxxxxxxxxxxxxxxxxxxx 000000000000000000000000 # SWR\n110000xxxxxxxxxxxxxxxxxxxxxxxxxx 000000000000000000000000 # LWC0\n110001xxxxxxxxxxxxxxxxxxxxxxxxxx 000000000000000000000000 # LWC1\n110010xxxxxxxxxxxxxxxxxxxxxxxxxx 000000000000000000000000 # LWC2\n110011xxxxxxxxxxxxxxxxxxxxxxxxxx 000000000000000000000000 # LWC3\n111000xxxxxxxxxxxxxxxxxxxxxxxxxx 000000000000000000000000 # SWC0\n111001xxxxxxxxxxxxxxxxxxxxxxxxxx 000000000000000000000000 # SWC1\n111010xxxxxxxxxxxxxxxxxxxxxxxxxx 000000000000000000000000 # SWC2\n111011xxxxxxxxxxxxxxxxxxxxxxxxxx 000000000000000000000000 # SWC3")) pla_1 (
    .in(Instr), .out(pla_1_out));
  PLA #(.in_width(32), .out_width(25), .\table ("000000xxxxxxxxxxxxxxxxxxxx000000 0000000000000000000000001 # SLL\n000000xxxxxxxxxxxxxxxxxxxx000010 0000000000000000000000010 # SRL\n000000xxxxxxxxxxxxxxxxxxxx000011 0000000000000000000000100 # SRA\n000000xxxxxxxxxxxxxxxxxxxx000100 0000000000000000000001000 # SLLV\n000000xxxxxxxxxxxxxxxxxxxx000110 0000000000000000000010000 # SRLV\n000000xxxxxxxxxxxxxxxxxxxx000111 0000000000000000000100000 # SRAV\n000000xxxxxxxxxxxxxxxxxxxx001000 0000000000000000001000000 # JR\n000000xxxxxxxxxxxxxxxxxxxx001001 0000000000000000010000000 # JALR\n000000xxxxxxxxxxxxxxxxxxxx001101 0000000000000000100000000 # BREAK\n000000xxxxxxxxxxxxxxxxxxxx010000 0000000000000001000000000 # MFHI\n000000xxxxxxxxxxxxxxxxxxxx010010 0000000000000010000000000 # MFLO\n000000xxxxxxxxxxxxxxxxxxxx011000 0000000000000100000000000 # MULT\n000000xxxxxxxxxxxxxxxxxxxx011001 0000000000001000000000000 # MULTU\n000000xxxxxxxxxxxxxxxxxxxx011010 0000000000010000000000000 # DIV\n000000xxxxxxxxxxxxxxxxxxxx011011 0000000000100000000000000 # DIVU\n000000xxxxxxxxxxxxxxxxxxxx100000 0000000001000000000000000 # ADD\n000000xxxxxxxxxxxxxxxxxxxx100001 0000000010000000000000000 # ADDU\n000000xxxxxxxxxxxxxxxxxxxx100010 0000000100000000000000000 # SUB\n000000xxxxxxxxxxxxxxxxxxxx100011 0000001000000000000000000 # SUBU\n000000xxxxxxxxxxxxxxxxxxxx100100 0000010000000000000000000 # AND\n000000xxxxxxxxxxxxxxxxxxxx100101 0000100000000000000000000 # OR\n000000xxxxxxxxxxxxxxxxxxxx100110 0001000000000000000000000 # XOR\n000000xxxxxxxxxxxxxxxxxxxx100111 0010000000000000000000000 # NOR\n000000xxxxxxxxxxxxxxxxxxxx101010 0100000000000000000000000 # SLT\n000000xxxxxxxxxxxxxxxxxxxx101011 1000000000000000000000000 # SLTU\n000000xxxxxxxxxxxxxxxxxxxxxxxxxx 0000000000000000000000000 # UNIMPL\n000000xxxxxxxxxxxxxxxxxxxx001100 0000000000000000000000000 # SYSCALL\n000000xxxxxxxxxxxxxxxxxxxx010001 0000000000000000000000000 # MTHI\n000000xxxxxxxxxxxxxxxxxxxx010011 0000000000000000000000000 # MTLO")) arith (
    .in(Instr), .out(arith_out));
  PLA #(.in_width(32), .out_width(4), .\table ("000001xxxxx00000xxxxxxxxxxxxxxxx 0001 # BLTZ\n000001xxxxx00001xxxxxxxxxxxxxxxx 0010 # BGEZ\n000001xxxxx10000xxxxxxxxxxxxxxxx 0100 # BLTZAL\n000001xxxxx10001xxxxxxxxxxxxxxxx 1000 # BGEZAL\n000001xxxxxxxxxxxxxxxxxxxxxxxxxx 0000 # UNIMPL")) regimm (
    .in(Instr), .out(regimm_out));
  PLA #(.in_width(32), .\table ("000000xxxxxxxxxxxxxxxxxxxx001000 10 # register # JR\n000000xxxxxxxxxxxxxxxxxxxx001001 10 # register # JALR\n000001xxxxx00000xxxxxxxxxxxxxxxx 01 # relative # BLTZ\n000001xxxxx00001xxxxxxxxxxxxxxxx 01 # relative # BGEZ\n000001xxxxx10000xxxxxxxxxxxxxxxx 01 # relative # BLTZAL\n000001xxxxx10001xxxxxxxxxxxxxxxx 01 # relative # BGEZAL\n000010xxxxxxxxxxxxxxxxxxxxxxxxxx 11 # absolute # J\n000011xxxxxxxxxxxxxxxxxxxxxxxxxx 11 # absolute # JAL\n000100xxxxxxxxxxxxxxxxxxxxxxxxxx 01 # relative # BEQ\n000101xxxxxxxxxxxxxxxxxxxxxxxxxx 01 # relative # BNE\n000110xxxxxxxxxxxxxxxxxxxxxxxxxx 01 # relative # BLEZ\n000111xxxxxxxxxxxxxxxxxxxxxxxxxx 01 # relative # BGTZ\nxxxxxxxxxxxxxxxxxxxxxxxxxxxxxxxx 00 # PC+4     # other")) NextPC (
    .in(Instr), .out(JS));
  PLA #(.in_width(32), .out_width(5), .\table ("000001xxxxx00000xxxxxxxxxxxxxxxx 00001 # BLTZ\n000001xxxxx00001xxxxxxxxxxxxxxxx 00110 # BGEZ\n000001xxxxx10000xxxxxxxxxxxxxxxx 00001 # BLTZAL\n000001xxxxx10001xxxxxxxxxxxxxxxx 00110 # BGEZAL\n000100xxxxxxxxxxxxxxxxxxxxxxxxxx 01000 # BEQ\n000101xxxxxxxxxxxxxxxxxxxxxxxxxx 10000 # BNE\n000110xxxxxxxxxxxxxxxxxxxxxxxxxx 00011 # BLEZ\n000111xxxxxxxxxxxxxxxxxxxxxxxxxx 00100 # BGTZ\nxxxxxxxxxxxxxxxxxxxxxxxxxxxxxxxx 00000 # ---")) branch (
    .in(Instr), .out(cond));
  PLA #(.in_width(32), .\table ("000000xxxxxxxxxxxxxxxxxxxx000000 00 # ---- # SLL\n000000xxxxxxxxxxxxxxxxxxxx000010 00 # ---- # SRL\n000000xxxxxxxxxxxxxxxxxxxx000011 00 # ---- # SRA\n000000xxxxxxxxxxxxxxxxxxxx000100 00 # reg  # SLLV\n000000xxxxxxxxxxxxxxxxxxxx000110 00 # reg  # SRLV\n000000xxxxxxxxxxxxxxxxxxxx000111 00 # reg  # SRAV\n000000xxxxxxxxxxxxxxxxxxxx001000 00 # ---- # JR\n000000xxxxxxxxxxxxxxxxxxxx001001 11 # pc+4 # JALR\n000000xxxxxxxxxxxxxxxxxxxx001101 00 # ---- # BREAK\n000000xxxxxxxxxxxxxxxxxxxx010000 00 # ---- # MFHI\n000000xxxxxxxxxxxxxxxxxxxx010010 00 # ---- # MFLO\n000000xxxxxxxxxxxxxxxxxxxx011000 00 # reg  # MULT\n000000xxxxxxxxxxxxxxxxxxxx011001 00 # reg  # MULTU\n000000xxxxxxxxxxxxxxxxxxxx011010 00 # reg  # DIV\n000000xxxxxxxxxxxxxxxxxxxx011011 00 # reg  # DIVU\n000000xxxxxxxxxxxxxxxxxxxx100000 00 # reg  # ADD\n000000xxxxxxxxxxxxxxxxxxxx100001 00 # reg  # ADDU\n000000xxxxxxxxxxxxxxxxxxxx100010 00 # reg  # SUB\n000000xxxxxxxxxxxxxxxxxxxx100011 00 # reg  # SUBU\n000000xxxxxxxxxxxxxxxxxxxx100100 00 # reg  # AND\n000000xxxxxxxxxxxxxxxxxxxx100101 00 # reg  # OR\n000000xxxxxxxxxxxxxxxxxxxx100110 00 # reg  # XOR\n000000xxxxxxxxxxxxxxxxxxxx100111 00 # reg  # NOR\n000000xxxxxxxxxxxxxxxxxxxx101010 00 # reg  # SLT\n000000xxxxxxxxxxxxxxxxxxxx101011 00 # reg  # SLTU\n000001xxxxx00000xxxxxxxxxxxxxxxx 00 # ---- # BLTZ\n000001xxxxx00001xxxxxxxxxxxxxxxx 00 # ---- # BGEZ\n000001xxxxx10000xxxxxxxxxxxxxxxx 11 # pc+4 # BLTZAL\n000001xxxxx10001xxxxxxxxxxxxxxxx 11 # pc+4 # BGEZAL\n000010xxxxxxxxxxxxxxxxxxxxxxxxxx 00 # ---- # J\n000011xxxxxxxxxxxxxxxxxxxxxxxxxx 11 # pc+4 # JAL\n000100xxxxxxxxxxxxxxxxxxxxxxxxxx 00 # ---- # BEQ\n000101xxxxxxxxxxxxxxxxxxxxxxxxxx 00 # ---- # BNE\n000110xxxxxxxxxxxxxxxxxxxxxxxxxx 00 # ---- # BLEZ\n000111xxxxxxxxxxxxxxxxxxxxxxxxxx 00 # ---- # BGTZ\n001000xxxxxxxxxxxxxxxxxxxxxxxxxx 10 # simm # ADDI\n001001xxxxxxxxxxxxxxxxxxxxxxxxxx 10 # simm # ADDIU\n001010xxxxxxxxxxxxxxxxxxxxxxxxxx 10 # simm # SLTI\n001011xxxxxxxxxxxxxxxxxxxxxxxxxx 10 # simm # SLTIU\n001100xxxxxxxxxxxxxxxxxxxxxxxxxx 01 # zimm # ANDI\n001101xxxxxxxxxxxxxxxxxxxxxxxxxx 01 # zimm # ORI\n001110xxxxxxxxxxxxxxxxxxxxxxxxxx 01 # zimm # XORI\n001111xxxxxxxxxxxxxxxxxxxxxxxxxx 01 # zimm # LUI\n100000xxxxxxxxxxxxxxxxxxxxxxxxxx 10 # simm # LB\n100001xxxxxxxxxxxxxxxxxxxxxxxxxx 10 # simm # LH\n100011xxxxxxxxxxxxxxxxxxxxxxxxxx 10 # simm # LW\n100100xxxxxxxxxxxxxxxxxxxxxxxxxx 10 # simm # LBU\n100101xxxxxxxxxxxxxxxxxxxxxxxxxx 10 # simm # LHU\n101000xxxxxxxxxxxxxxxxxxxxxxxxxx 10 # simm # SB\n101001xxxxxxxxxxxxxxxxxxxxxxxxxx 10 # simm # SH\n101011xxxxxxxxxxxxxxxxxxxxxxxxxx 10 # simm # SW\nxxxxxxxxxxxxxxxxxxxxxxxxxxxxxxxx 00 # ---- # ?")) immsel (
    .in(Instr), .out(CS));
  PLA #(.in_width(32), .out_width(5), .\table ("000000xxxxxxxxxxxxxxxxxxxx000000 01001 # SLL\n000000xxxxxxxxxxxxxxxxxxxx000010 01010 # SRL\n000000xxxxxxxxxxxxxxxxxxxx000011 01011 # SRA\n000000xxxxxxxxxxxxxxxxxxxx000100 01100 # SLLV\n000000xxxxxxxxxxxxxxxxxxxx000110 01101 # SRLV\n000000xxxxxxxxxxxxxxxxxxxx000111 01110 # SRAV\n000000xxxxxxxxxxxxxxxxxxxx001000 00000 # ----- # JR\n000000xxxxxxxxxxxxxxxxxxxx001001 10000 # Y     # JALR\n000000xxxxxxxxxxxxxxxxxxxx001101 00000 # ----- # BREAK\n000000xxxxxxxxxxxxxxxxxxxx010000 10001 # ----- # MFHI\n000000xxxxxxxxxxxxxxxxxxxx010010 10010 # ----- # MFLO\n000000xxxxxxxxxxxxxxxxxxxx011000 11000 # MULT\n000000xxxxxxxxxxxxxxxxxxxx011001 11001 # MULTU\n000000xxxxxxxxxxxxxxxxxxxx011010 11010 # DIV\n000000xxxxxxxxxxxxxxxxxxxx011011 11011 # DIVU\n000000xxxxxxxxxxxxxxxxxxxx100000 00001 # ADD\n000000xxxxxxxxxxxxxxxxxxxx100001 00001 # ADD   # ADDU\n000000xxxxxxxxxxxxxxxxxxxx100010 00010 # SUB\n000000xxxxxxxxxxxxxxxxxxxx100011 00010 # SUB   # SUBU\n000000xxxxxxxxxxxxxxxxxxxx100100 00011 # AND\n000000xxxxxxxxxxxxxxxxxxxx100101 00100 # OR\n000000xxxxxxxxxxxxxxxxxxxx100110 00101 # XOR\n000000xxxxxxxxxxxxxxxxxxxx100111 00110 # NOR\n000000xxxxxxxxxxxxxxxxxxxx101010 00111 # LESS  # SLT\n000000xxxxxxxxxxxxxxxxxxxx101011 01000 # LESSU # SLTU\n000001xxxxx00000xxxxxxxxxxxxxxxx 00000 # ----- # BLTZ\n000001xxxxx00001xxxxxxxxxxxxxxxx 00000 # ----- # BGEZ\n000001xxxxx10000xxxxxxxxxxxxxxxx 10000 # Y     # BLTZAL\n000001xxxxx10001xxxxxxxxxxxxxxxx 10000 # Y     # BGEZAL\n000010xxxxxxxxxxxxxxxxxxxxxxxxxx 00000 # ----- # J\n000011xxxxxxxxxxxxxxxxxxxxxxxxxx 10000 # Y     # JAL\n000100xxxxxxxxxxxxxxxxxxxxxxxxxx 00000 # ----- # BEQ\n000101xxxxxxxxxxxxxxxxxxxxxxxxxx 00000 # ----- # BNE\n000110xxxxxxxxxxxxxxxxxxxxxxxxxx 00000 # ----- # BLEZ\n000111xxxxxxxxxxxxxxxxxxxxxxxxxx 00000 # ----- # BGTZ\n001000xxxxxxxxxxxxxxxxxxxxxxxxxx 00001 # ADD   # ADDI\n001001xxxxxxxxxxxxxxxxxxxxxxxxxx 00001 # ADD   # ADDIU\n001010xxxxxxxxxxxxxxxxxxxxxxxxxx 00111 # LESS  # SLTI\n001011xxxxxxxxxxxxxxxxxxxxxxxxxx 01000 # LESSU # SLTIU\n001100xxxxxxxxxxxxxxxxxxxxxxxxxx 00011 # AND   # ANDI\n001101xxxxxxxxxxxxxxxxxxxxxxxxxx 00100 # OR    # ORI\n001110xxxxxxxxxxxxxxxxxxxxxxxxxx 00101 # XOR   # XORI\n001111xxxxxxxxxxxxxxxxxxxxxxxxxx 01111 # SWAPY # LUI\n100000xxxxxxxxxxxxxxxxxxxxxxxxxx 00001 # ADD   # LB\n100001xxxxxxxxxxxxxxxxxxxxxxxxxx 00001 # ADD   # LH\n100011xxxxxxxxxxxxxxxxxxxxxxxxxx 00001 # ADD   # LW\n100100xxxxxxxxxxxxxxxxxxxxxxxxxx 00001 # ADD   # LBU\n100101xxxxxxxxxxxxxxxxxxxxxxxxxx 00001 # ADD   # LHU\n101000xxxxxxxxxxxxxxxxxxxxxxxxxx 00001 # ADD   # SB\n101001xxxxxxxxxxxxxxxxxxxxxxxxxx 00001 # ADD   # SH\n101011xxxxxxxxxxxxxxxxxxxxxxxxxx 00001 # ADD   # SW\nxxxxxxxxxxxxxxxxxxxxxxxxxxxxxxxx 00000 # ----- # ?")) pla_2 (
    .in(Instr), .out(AluOp));
  PLA #(.in_width(32), .out_width(1), .\table ("100000xxxxxxxxxxxxxxxxxxxxxxxxxx 1 # mem   # LB\n100001xxxxxxxxxxxxxxxxxxxxxxxxxx 1 # mem   # LH\n100011xxxxxxxxxxxxxxxxxxxxxxxxxx 1 # mem   # LW\n100100xxxxxxxxxxxxxxxxxxxxxxxxxx 1 # mem   # LBU\n100101xxxxxxxxxxxxxxxxxxxxxxxxxx 1 # mem   # LHU\nxxxxxxxxxxxxxxxxxxxxxxxxxxxxxxxx 0 # ---   # ?")) result (
    .in(Instr), .out(RS));
  PLA #(.in_width(32), .out_width(4), .\table ("000000xxxxxxxxxxxxxxxxxxxx000000 1101 # rd -- rt # SLL\n000000xxxxxxxxxxxxxxxxxxxx000010 1101 # rd -- rt # SRL\n000000xxxxxxxxxxxxxxxxxxxx000011 1101 # rd -- rt # SRA\n000000xxxxxxxxxxxxxxxxxxxx000100 1111 # rd rs rt # SLLV\n000000xxxxxxxxxxxxxxxxxxxx000110 1111 # rd rs rt # SRLV\n000000xxxxxxxxxxxxxxxxxxxx000111 1111 # rd rs rt # SRAV\n000000xxxxxxxxxxxxxxxxxxxx001000 0010 # -- rs -- # JR\n000000xxxxxxxxxxxxxxxxxxxx001001 1110 # rd rs -- # JALR\n000000xxxxxxxxxxxxxxxxxxxx001101 0000 # -- -- -- # BREAK\n000000xxxxxxxxxxxxxxxxxxxx010000 1100 # rd -- -- # MFHI\n000000xxxxxxxxxxxxxxxxxxxx010010 1100 # rd -- -- # MFLO\n000000xxxxxxxxxxxxxxxxxxxx011000 0011 # -- rs rt # MULT\n000000xxxxxxxxxxxxxxxxxxxx011001 0011 # -- rs rt # MULTU\n000000xxxxxxxxxxxxxxxxxxxx011010 0011 # -- rs rt # DIV\n000000xxxxxxxxxxxxxxxxxxxx011011 0011 # -- rs rt # DIVU\n000000xxxxxxxxxxxxxxxxxxxx100000 1111 # rd rs rt # ADD\n000000xxxxxxxxxxxxxxxxxxxx100001 1111 # rd rs rt # ADDU\n000000xxxxxxxxxxxxxxxxxxxx100010 1111 # rd rs rt # SUB\n000000xxxxxxxxxxxxxxxxxxxx100011 1111 # rd rs rt # SUBU\n000000xxxxxxxxxxxxxxxxxxxx100100 1111 # rd rs rt # AND\n000000xxxxxxxxxxxxxxxxxxxx100101 1111 # rd rs rt # OR\n000000xxxxxxxxxxxxxxxxxxxx100110 1111 # rd rs rt # XOR\n000000xxxxxxxxxxxxxxxxxxxx100111 1111 # rd rs rt # NOR\n000000xxxxxxxxxxxxxxxxxxxx101010 1111 # rd rs rt # SLT\n000000xxxxxxxxxxxxxxxxxxxx101011 1111 # rd rs rt # SLTU\n000001xxxxx00000xxxxxxxxxxxxxxxx 0010 # -- rs -- # BLTZ\n000001xxxxx00001xxxxxxxxxxxxxxxx 0010 # -- rs -- # BGEZ\n000001xxxxx10000xxxxxxxxxxxxxxxx 0110 # 31 rs -- # BLTZAL\n000001xxxxx10001xxxxxxxxxxxxxxxx 0110 # 31 rs -- # BGEZAL\n000010xxxxxxxxxxxxxxxxxxxxxxxxxx 0000 # -- -- -- # J\n000011xxxxxxxxxxxxxxxxxxxxxxxxxx 0100 # 31 -- -- # JAL\n000100xxxxxxxxxxxxxxxxxxxxxxxxxx 0011 # -- rs rt # BEQ\n000101xxxxxxxxxxxxxxxxxxxxxxxxxx 0011 # -- rs rt # BNE\n000110xxxxxxxxxxxxxxxxxxxxxxxxxx 0010 # -- rs -- # BLEZ\n000111xxxxxxxxxxxxxxxxxxxxxxxxxx 0010 # -- rs -- # BGTZ\n001000xxxxxxxxxxxxxxxxxxxxxxxxxx 1010 # rt rs -- # ADDI\n001001xxxxxxxxxxxxxxxxxxxxxxxxxx 1010 # rt rs -- # ADDIU\n001010xxxxxxxxxxxxxxxxxxxxxxxxxx 1010 # rt rs -- # SLTI\n001011xxxxxxxxxxxxxxxxxxxxxxxxxx 1010 # rt rs -- # SLTIU\n001100xxxxxxxxxxxxxxxxxxxxxxxxxx 1010 # rt rs -- # ANDI\n001101xxxxxxxxxxxxxxxxxxxxxxxxxx 1010 # rt rs -- # ORI\n001110xxxxxxxxxxxxxxxxxxxxxxxxxx 1010 # rt rs -- # XORI\n001111xxxxxxxxxxxxxxxxxxxxxxxxxx 1000 # rt -- -- # LUI\n100000xxxxxxxxxxxxxxxxxxxxxxxxxx 1010 # rt rs -- # LB\n100001xxxxxxxxxxxxxxxxxxxxxxxxxx 1010 # rt rs -- # LH\n100011xxxxxxxxxxxxxxxxxxxxxxxxxx 1010 # rt rs -- # LW\n100100xxxxxxxxxxxxxxxxxxxxxxxxxx 1010 # rt rs -- # LBU\n100101xxxxxxxxxxxxxxxxxxxxxxxxxx 1010 # rt rs -- # LHU\n101000xxxxxxxxxxxxxxxxxxxxxxxxxx 0011 # -- rs rt # SB\n101001xxxxxxxxxxxxxxxxxxxxxxxxxx 0011 # -- rs rt # SH\n101011xxxxxxxxxxxxxxxxxxxxxxxxxx 0011 # -- rs rt # SW\nxxxxxxxxxxxxxxxxxxxxxxxxxxxxxxxx 0000 # -- -- -- # ?")) regsel (
    .in(Instr), .out(regsel_out));
  PLA #(.in_width(32), .out_width(5), .\table ("100000xxxxxxxxxxxxxxxxxxxxxxxxxx 01001 # LB\n100001xxxxxxxxxxxxxxxxxxxxxxxxxx 01101 # LH\n100011xxxxxxxxxxxxxxxxxxxxxxxxxx 01010 # LW\n100100xxxxxxxxxxxxxxxxxxxxxxxxxx 01000 # LBU\n100101xxxxxxxxxxxxxxxxxxxxxxxxxx 01100 # LHU\n101000xxxxxxxxxxxxxxxxxxxxxxxxxx 10000 # SB\n101001xxxxxxxxxxxxxxxxxxxxxxxxxx 10100 # SH\n101011xxxxxxxxxxxxxxxxxxxxxxxxxx 10010 # SW\nxxxxxxxxxxxxxxxxxxxxxxxxxxxxxxxx 00000 # --")) memory (
    .in(Instr), .out({MWrite, MRead, MHalf, MWord, MSigned}));
  // Probe on Instr[31:26]
  // Probe on Instr[25:21]
  // Probe on Instr[20:16]
  // Probe on Instr[15:11]
  // Probe on Instr[10:6]
  // Probe on Instr[5:0]
  assign ZI = {{16{1'b0}}, Instr[15:0]};  // Bit_Extender bit_extender_1
  assign SI = {{16{Instr[15]}}, Instr[15:0]};  // Bit_Extender bit_extender_2
  assign PCAbsolute = {{4{1'b0}}, {Instr[25:0], 2'b00}};  // Bit_Extender bit_extender_3
  Multiplexer #(.select(2), .width(5)) multiplexer_1 (
    .in0({5{1'b0}}), .in1({5{1'b1}}), .in2(Instr[20:16]), .in3(Instr[15:11]), .out(DS), .sel(regsel_out[3:2]));
  Multiplexer #(.width(5)) multiplexer_2 (.in0({5{1'b0}}), .in1(Instr[25:21]), .out(XS), .sel(regsel_out[1]));
  LED BLTZ (.in(regimm_out[0]));
  LED BGEZ (.in(regimm_out[1]));
  LED BLTZAL (.in(regimm_out[2]));
  LED BGEZAL (.in(regimm_out[3]));
  Multiplexer #(.width(5)) multiplexer_3 (.in0({5{1'b0}}), .in1(Instr[20:16]), .out(YS), .sel(regsel_out[0]));
  LED SLL (.in(arith_out[0]));
  LED SRL (.in(arith_out[1]));
  LED SRA (.in(arith_out[2]));
  LED SLLV (.in(arith_out[3]));
  LED SRLV (.in(arith_out[4]));
  LED SRAV (.in(arith_out[5]));
  LED JR (.in(arith_out[6]));
  LED JALR (.in(arith_out[7]));
  LED BREAK (.in(arith_out[8]));
  LED MFHI (.in(arith_out[9]));
  LED MFLO (.in(arith_out[10]));
  LED MULT (.in(arith_out[11]));
  LED MULTU (.in(arith_out[12]));
  LED DIV (.in(arith_out[13]));
  LED DIVU (.in(arith_out[14]));
  LED ADD (.in(arith_out[15]));
  LED ADDU (.in(arith_out[16]));
  LED SUB (.in(arith_out[17]));
  LED SUBU (.in(arith_out[18]));
  LED AND (.in(arith_out[19]));
  LED OR (.in(arith_out[20]));
  LED XOR (.in(arith_out[21]));
  LED NOR (.in(arith_out[22]));
  LED SLT (.in(arith_out[23]));
  LED SLTU (.in(arith_out[24]));
  LED led_1 (.in(pla_1_out[0]));
  LED led_2 (.in(pla_1_out[1]));
  LED J (.in(pla_1_out[2]));
  LED JAL (.in(pla_1_out[3]));
  LED BEQ (.in(pla_1_out[4]));
  LED BNE (.in(pla_1_out[5]));
  LED BLEZ (.in(pla_1_out[6]));
  LED BGTZ (.in(pla_1_out[7]));
  LED ADDI (.in(pla_1_out[8]));
  LED ADDIU (.in(pla_1_out[9]));
  LED SLTI (.in(pla_1_out[10]));
  LED SLTIU (.in(pla_1_out[11]));
  LED ANDI (.in(pla_1_out[12]));
  LED ORI (.in(pla_1_out[13]));
  LED XORI (.in(pla_1_out[14]));
  LED LUI (.in(pla_1_out[15]));
  LED LB (.in(pla_1_out[16]));
  LED LH (.in(pla_1_out[17]));
  LED LW (.in(pla_1_out[18]));
  LED LBU (.in(pla_1_out[19]));
  LED LHU (.in(pla_1_out[20]));
  LED SB (.in(pla_1_out[21]));
  LED SH (.in(pla_1_out[22]));
  LED SW (.in(pla_1_out[23]));

  assign out_12 = Instr[10:6];

  // Notes on the sheet:
  //   based on opcode, decide which instruction
  //   Jump selector controls the PC mux
  //   Register selector, used to decide which (if any) registers are used.
  //   based on lower 6 bits, decide which arithmetic instruction
  //   based on various bits, decide which branch instruction
  //   Constant selector, used for selecting the second ALU operand.
  //   Result selector, used to control the mux near the end of the datapath.
  //   Shift amount, for some shift instructions.
  //   Zero-extended immediate
  //   Sign-extended immediate
  //   Branch cond, used to control the branch calculation component.
  //   Target for absolute jumps
  //   These LEDs are just for show currently... but it may be usefulin future to be able to detect specific individual instructions.
  //   Memory control signals, used to control the northbridge.
  //   Dest, X, and Y register selectors. These will bezero for instructions that don't use thatparticular register (e.g. Branches don'twrite to a register, so DS will be zero for branches).Otherwise, they will contain the registernumbers (0-31) used by the instruction.
endmodule

module branchcalc (
  input  [31:0] X,
  input  [31:0] Y,
  input  [4:0] cond,
  input  [31:0] SImm,
  output [31:0] BrOffset
);

  wire and_1_out, and_2_out, and_3_out, and_4_out, and_5_out, comparator_1_eq, comparator_2_eq,
       comparator_2_gt, comparator_2_lt, not_1_out, or_1_out;
  wire [31:0] multiplexer_1_out, shifter_1_out;

  Comparator #(.width(32)) comparator_1 (.a(X), .b(Y), .eq(comparator_1_eq));  // open: gt, lt
  not not_1 (not_1_out, comparator_1_eq);
  Comparator #(.width(32)) comparator_2 (
    .a(X), .b({32{1'b0}}), .gt(comparator_2_gt), .eq(comparator_2_eq), .lt(comparator_2_lt));
  and and_1 (and_1_out, not_1_out, cond[4]);
  and and_2 (and_2_out, comparator_1_eq, cond[3]);
  and and_3 (and_3_out, comparator_2_gt, cond[2]);
  or or_1 (or_1_out, and_1_out, and_2_out, and_3_out, and_4_out, and_5_out);
  Multiplexer #(.width(32)) multiplexer_1 (
    .in0({32{1'b0}}), .in1(shifter_1_out), .out(multiplexer_1_out), .sel(or_1_out));
  plusfour plusfour_1 (.A(multiplexer_1_out), .V(BrOffset));
  and and_4 (and_4_out, comparator_2_eq, cond[1]);
  and and_5 (and_5_out, comparator_2_lt, cond[0]);
  Shifter #(.width(32)) shifter_1 (.in(SImm), .\dist (5'b00010), .out(shifter_1_out));

  // Notes on the sheet:
  //   N
  //   E
  //   G
  //   L
  //   Z
  //   # The branch calculation component supports five different conditions:
  //   #   xxxxL - branch if X is less than zero
  //   #   xxxZx - branch if X is zero
  //   #   xxGxx - branch if X is greater than zero
  //   #   xExxx - branch if X is equal to Y
  //   #   Nxxxx - branch if X is not equal to Y
  //   # Each branch instruction enables one or more of those conditions.
endmodule

module ALU (
  input  [31:0] X,
  input  [31:0] Y,
  input  [4:0] sh,
  input  [4:0] Op,
  input  CLK,
  output [31:0] R
);

  wire comparator_1_lt, comparator_2_lt, whilo;
  wire [4:0] multiplexer_1_out;
  wire [31:0] adder_1_out, and_1_out, bit_extender_1_out, bit_extender_2_out, divider_1_out, divider_1_rem,
       divider_2_out, divider_2_rem, hi_q, lo_q, multiplexer_2_out, multiplexer_3_out, multiplexer_4_out,
       multiplier_1_cout, multiplier_1_out, multiplier_2_cout, multiplier_2_out, nor_1_out, not_1_out,
       or_1_out, shifter_1_out, shifter_2_out, shifter_3_out, xor_1_out;

  Multiplexer #(.width(5)) multiplexer_1 (.in0(sh), .in1(X[4:0]), .out(multiplexer_1_out), .sel(Op[2]));
  assign not_1_out = ~Y;  // NOT_Gate not_1, 32 bits wide
  Multiplier #(.width(32)) multiplier_1 (.a(X), .b(Y), .out(multiplier_1_out), .cout(multiplier_1_cout));  // open: cin
  Multiplier #(.width(32)) multiplier_2 (.a(X), .b(Y), .out(multiplier_2_out), .cout(multiplier_2_cout));  // open: cin
  Divider #(.width(32)) divider_1 (.a(X), .b(Y), .out(divider_1_out), .rem(divider_1_rem));  // open: upper
  Divider #(.width(32)) divider_2 (.a(X), .b(Y), .out(divider_2_out), .rem(divider_2_rem));  // open: upper
  Multiplexer #(.width(32)) multiplexer_2 (.in0(Y), .in1(not_1_out), .out(multiplexer_2_out), .sel(Op[1]));
  Adder #(.width(32)) adder_1 (.a(X), .b(multiplexer_2_out), .out(adder_1_out), .cin(Op[1]));  // open: cout
  assign and_1_out = X & Y;  // AND_Gate and_1, 32 bits wide
  assign or_1_out = X | Y;  // OR_Gate or_1, 32 bits wide
  assign xor_1_out = X ^ Y;  // XOR_Gate xor_1, 32 bits wide
  assign nor_1_out = ~(X | Y);  // NOR_Gate nor_1, 32 bits wide
  Comparator #(.width(32)) comparator_1 (.a(X), .b(Y), .lt(comparator_1_lt));  // open: gt, eq
  Comparator #(.mode("unsigned"), .width(32)) comparator_2 (.a(X), .b(Y), .lt(comparator_2_lt));  // open: gt, eq
  Shifter #(.width(32)) shifter_1 (.in(Y), .\dist (multiplexer_1_out), .out(shifter_1_out));
  Shifter #(.shift("lr"), .width(32)) shifter_2 (.in(Y), .\dist (multiplexer_1_out), .out(shifter_2_out));
  Shifter #(.shift("ar"), .width(32)) shifter_3 (.in(Y), .\dist (multiplexer_1_out), .out(shifter_3_out));
  Multiplexer #(.select(2), .width(32)) multiplexer_3 (
    .in0(multiplier_1_out), .in1(multiplier_2_out), .in2(divider_1_rem), .in3(divider_2_rem),
    .out(multiplexer_3_out), .sel(Op[1:0]));
  Multiplexer #(.select(2), .width(32)) multiplexer_4 (
    .in0(multiplier_1_cout), .in1(multiplier_2_cout), .in2(divider_1_out), .in3(divider_2_out),
    .out(multiplexer_4_out), .sel(Op[1:0]));
  assign bit_extender_1_out = {{31{1'b0}}, comparator_1_lt};  // Bit_Extender bit_extender_1
  assign bit_extender_2_out = {{31{1'b0}}, comparator_2_lt};  // Bit_Extender bit_extender_2
  Register #(.width(32)) lo (.D(multiplexer_3_out), .en(whilo), .Q(lo_q), .clk(CLK));  // open: clr
  Register #(.width(32)) hi (.D(multiplexer_4_out), .en(whilo), .Q(hi_q), .clk(CLK));  // open: clr
  Multiplexer #(.select(5), .width(32)) multiplexer_5 (
    .in0({32{1'b0}}), .in1(adder_1_out), .in2(adder_1_out), .in3(and_1_out), .in4(or_1_out), .in5(xor_1_out),
    .in6(nor_1_out), .in7(bit_extender_1_out), .in8(bit_extender_2_out), .in9(shifter_1_out),
    .in10(shifter_2_out), .in11(shifter_3_out), .in12(shifter_1_out), .in13(shifter_2_out),
    .in14(shifter_3_out), .in15({Y[15:0], Y[31:16]}), .in16(Y), .in17(hi_q), .in18(lo_q), .in19({32{1'b0}}),
    .in20({32{1'b0}}), .in21({32{1'b0}}), .in22({32{1'b0}}), .in23({32{1'b0}}), .in24({32{1'b0}}),
    .in25({32{1'b0}}), .in26({32{1'b0}}), .in27({32{1'b0}}), .in28({32{1'b0}}), .in29({32{1'b0}}),
    .in30({32{1'b0}}), .in31({32{1'b0}}), .out(R), .sel(Op));
  and and_2 (whilo, Op[3], Op[4]);

  // Other names for the same wires on the sheet: mulsel[1:0] = Op[1:0]; sub = Op[1]; varshift = Op[2]

  // Notes on the sheet:
  //   # The ALU supports these operations:
  //   #    11011 means divu (hi = X / Y; lo = X % Y)
  //   #    11010 means div (hi = X / Y; lo = X % Y)
  //   #    01110 means shift-right-arithmetic-variable (R = Y >>> Y)
  //   #    01000 means less-than-unsigned (R = X < Y ? 1 : 0)
  //   #    01100 means shift-left-logical-variable (R = Y << X)
  //   #    01001 means shift-left-logical (R = Y << sh)
  //   #    01011 means shift-right-arithmetic (R = Y >>> sh)
  //   #    01010 means shift-right-logical (R = Y >> sh)
  //   #    01101 means shift-right-logical-variable (R = Y >> X)
  //   #    01111 means swap-y (R = upperhalf(Y):lowerhalf(Y)
  //   #    10010 means mflo (R = lo)
  //   #    11000 means mult (hi:lo = X * Y)
  //   #    11001 means multu (hi:lo = X * Y)
  //   #    10000 means y (R = Y)
  //   #    00000 means zero (R = 0)
  //   #    00001 means add (R = X + Y)
  //   #    00010 means sub (R = X - Y)
  //   #    00011 means and (R = X & Y)
  //   #    00100 means or (R = X | Y)
  //   #    00101 means xor (R = X ^ Y)
  //   #    00110 means nor (R = ~(X | Y))
  //   #    00111 means less-than (R = X < Y ? 1 : 0)
endmodule

module regfile (
  input  [31:0] D,
  input  [4:0] DS,
  input  [4:0] XS,
  input  clk,
  input  [4:0] YS,
  output [31:0] X,
  output [31:0] Y
);

  wire decoder_2_out0, decoder_2_out1, decoder_2_out2, decoder_2_out3, decoder_2_out4, decoder_2_out5,
       decoder_2_out6, decoder_2_out7, decoder_2_out8, decoder_2_out9, decoder_2_out10, decoder_2_out11,
       decoder_2_out12, decoder_2_out13, decoder_2_out14, decoder_2_out15, decoder_2_out16, decoder_2_out17,
       decoder_2_out18, decoder_2_out19, decoder_2_out20, decoder_2_out21, decoder_2_out22, decoder_2_out23,
       decoder_2_out24, decoder_2_out25, decoder_2_out26, decoder_2_out27, decoder_2_out28, decoder_2_out29,
       decoder_2_out30, decoder_2_out31, decoder_3_out0, decoder_3_out1, decoder_3_out2, decoder_3_out3,
       decoder_3_out4, decoder_3_out5, decoder_3_out6, decoder_3_out7, decoder_3_out8, decoder_3_out9,
       decoder_3_out10, decoder_3_out11, decoder_3_out12, decoder_3_out13, decoder_3_out14, decoder_3_out15,
       decoder_3_out16, decoder_3_out17, decoder_3_out18, decoder_3_out19, decoder_3_out20, decoder_3_out21,
       decoder_3_out22, decoder_3_out23, decoder_3_out24, decoder_3_out25, decoder_3_out26, decoder_3_out27,
       decoder_3_out28, decoder_3_out29, decoder_3_out30, decoder_3_out31;
  wire [31:0] decoder_1_out0, register_1_q, register_2_q, register_3_q, register_4_q, register_5_q,
       register_6_q, register_7_q, register_8_q, register_9_q, register_10_q, register_11_q, register_12_q,
       register_13_q, register_14_q, register_15_q, register_16_q, register_17_q, register_18_q,
       register_19_q, register_20_q, register_21_q, register_22_q, register_23_q, register_24_q,
       register_25_q, register_26_q, register_27_q, register_28_q, register_29_q, register_30_q,
       register_31_q;

  Decoder #(.enable("false"), .select(5)) decoder_1 (
    .out0(decoder_1_out0[0]), .out1(decoder_1_out0[1]), .out2(decoder_1_out0[2]), .out3(decoder_1_out0[3]),
    .out4(decoder_1_out0[4]), .out5(decoder_1_out0[5]), .out6(decoder_1_out0[6]), .out7(decoder_1_out0[7]),
    .out8(decoder_1_out0[8]), .out9(decoder_1_out0[9]), .out10(decoder_1_out0[10]),
    .out11(decoder_1_out0[11]), .out12(decoder_1_out0[12]), .out13(decoder_1_out0[13]),
    .out14(decoder_1_out0[14]), .out15(decoder_1_out0[15]), .out16(decoder_1_out0[16]),
    .out17(decoder_1_out0[17]), .out18(decoder_1_out0[18]), .out19(decoder_1_out0[19]),
    .out20(decoder_1_out0[20]), .out21(decoder_1_out0[21]), .out22(decoder_1_out0[22]),
    .out23(decoder_1_out0[23]), .out24(decoder_1_out0[24]), .out25(decoder_1_out0[25]),
    .out26(decoder_1_out0[26]), .out27(decoder_1_out0[27]), .out28(decoder_1_out0[28]),
    .out29(decoder_1_out0[29]), .out30(decoder_1_out0[30]), .out31(decoder_1_out0[31]), .sel(DS));
  LED led_1 (.in(decoder_1_out0[0]));
  LED led_2 (.in(decoder_1_out0[1]));
  LED led_3 (.in(decoder_1_out0[2]));
  LED led_4 (.in(decoder_1_out0[3]));
  LED led_5 (.in(decoder_1_out0[4]));
  LED led_6 (.in(decoder_1_out0[5]));
  LED led_7 (.in(decoder_1_out0[6]));
  LED led_8 (.in(decoder_1_out0[7]));
  LED led_9 (.in(decoder_1_out0[8]));
  LED led_10 (.in(decoder_1_out0[9]));
  LED led_11 (.in(decoder_1_out0[10]));
  LED led_12 (.in(decoder_1_out0[11]));
  LED led_13 (.in(decoder_1_out0[12]));
  LED led_14 (.in(decoder_1_out0[13]));
  LED led_15 (.in(decoder_1_out0[14]));
  LED led_16 (.in(decoder_1_out0[15]));
  LED led_17 (.in(decoder_1_out0[16]));
  LED led_18 (.in(decoder_1_out0[17]));
  LED led_19 (.in(decoder_1_out0[18]));
  LED led_20 (.in(decoder_1_out0[19]));
  LED led_21 (.in(decoder_1_out0[20]));
  LED led_22 (.in(decoder_1_out0[21]));
  LED led_23 (.in(decoder_1_out0[22]));
  LED led_24 (.in(decoder_1_out0[23]));
  LED led_25 (.in(decoder_1_out0[24]));
  LED led_26 (.in(decoder_1_out0[25]));
  LED led_27 (.in(decoder_1_out0[26]));
  LED led_28 (.in(decoder_1_out0[27]));
  LED led_29 (.in(decoder_1_out0[28]));
  LED led_30 (.in(decoder_1_out0[29]));
  LED led_31 (.in(decoder_1_out0[30]));
  LED led_32 (.in(decoder_1_out0[31]));
  Register #(.width(32)) register_1 (.D(D), .en(decoder_1_out0[1]), .Q(register_1_q), .clk(clk));  // open: clr
  Register #(.width(32)) register_2 (.D(D), .en(decoder_1_out0[2]), .Q(register_2_q), .clk(clk));  // open: clr
  Register #(.width(32)) register_3 (.D(D), .en(decoder_1_out0[3]), .Q(register_3_q), .clk(clk));  // open: clr
  Register #(.width(32)) register_4 (.D(D), .en(decoder_1_out0[4]), .Q(register_4_q), .clk(clk));  // open: clr
  Register #(.width(32)) register_5 (.D(D), .en(decoder_1_out0[5]), .Q(register_5_q), .clk(clk));  // open: clr
  Register #(.width(32)) register_6 (.D(D), .en(decoder_1_out0[6]), .Q(register_6_q), .clk(clk));  // open: clr
  Register #(.width(32)) register_7 (.D(D), .en(decoder_1_out0[7]), .Q(register_7_q), .clk(clk));  // open: clr
  Register #(.width(32)) register_8 (.D(D), .en(decoder_1_out0[8]), .Q(register_8_q), .clk(clk));  // open: clr
  Register #(.width(32)) register_9 (.D(D), .en(decoder_1_out0[9]), .Q(register_9_q), .clk(clk));  // open: clr
  Register #(.width(32)) register_10 (.D(D), .en(decoder_1_out0[10]), .Q(register_10_q), .clk(clk));  // open: clr
  Register #(.width(32)) register_11 (.D(D), .en(decoder_1_out0[11]), .Q(register_11_q), .clk(clk));  // open: clr
  Register #(.width(32)) register_12 (.D(D), .en(decoder_1_out0[12]), .Q(register_12_q), .clk(clk));  // open: clr
  Register #(.width(32)) register_13 (.D(D), .en(decoder_1_out0[13]), .Q(register_13_q), .clk(clk));  // open: clr
  Register #(.width(32)) register_14 (.D(D), .en(decoder_1_out0[14]), .Q(register_14_q), .clk(clk));  // open: clr
  Register #(.width(32)) register_15 (.D(D), .en(decoder_1_out0[15]), .Q(register_15_q), .clk(clk));  // open: clr
  Register #(.width(32)) register_16 (.D(D), .en(decoder_1_out0[16]), .Q(register_16_q), .clk(clk));  // open: clr
  Register #(.width(32)) register_17 (.D(D), .en(decoder_1_out0[17]), .Q(register_17_q), .clk(clk));  // open: clr
  Register #(.width(32)) register_18 (.D(D), .en(decoder_1_out0[18]), .Q(register_18_q), .clk(clk));  // open: clr
  Register #(.width(32)) register_19 (.D(D), .en(decoder_1_out0[19]), .Q(register_19_q), .clk(clk));  // open: clr
  Register #(.width(32)) register_20 (.D(D), .en(decoder_1_out0[20]), .Q(register_20_q), .clk(clk));  // open: clr
  Register #(.width(32)) register_21 (.D(D), .en(decoder_1_out0[21]), .Q(register_21_q), .clk(clk));  // open: clr
  Register #(.width(32)) register_22 (.D(D), .en(decoder_1_out0[22]), .Q(register_22_q), .clk(clk));  // open: clr
  Register #(.width(32)) register_23 (.D(D), .en(decoder_1_out0[23]), .Q(register_23_q), .clk(clk));  // open: clr
  Register #(.width(32)) register_24 (.D(D), .en(decoder_1_out0[24]), .Q(register_24_q), .clk(clk));  // open: clr
  Register #(.width(32)) register_25 (.D(D), .en(decoder_1_out0[25]), .Q(register_25_q), .clk(clk));  // open: clr
  Register #(.width(32)) register_26 (.D(D), .en(decoder_1_out0[26]), .Q(register_26_q), .clk(clk));  // open: clr
  Register #(.width(32)) register_27 (.D(D), .en(decoder_1_out0[27]), .Q(register_27_q), .clk(clk));  // open: clr
  Register #(.width(32)) register_28 (.D(D), .en(decoder_1_out0[28]), .Q(register_28_q), .clk(clk));  // open: clr
  Register #(.width(32)) register_29 (.D(D), .en(decoder_1_out0[29]), .Q(register_29_q), .clk(clk));  // open: clr
  Register #(.width(32)) register_30 (.D(D), .en(decoder_1_out0[30]), .Q(register_30_q), .clk(clk));  // open: clr
  Register #(.width(32)) register_31 (.D(D), .en(decoder_1_out0[31]), .Q(register_31_q), .clk(clk));  // open: clr
  Multiplexer #(.select(5), .width(32)) multiplexer_1 (
    .in0({32{1'b0}}), .in1(register_1_q), .in2(register_2_q), .in3(register_3_q), .in4(register_4_q),
    .in5(register_5_q), .in6(register_6_q), .in7(register_7_q), .in8(register_8_q), .in9(register_9_q),
    .in10(register_10_q), .in11(register_11_q), .in12(register_12_q), .in13(register_13_q),
    .in14(register_14_q), .in15(register_15_q), .in16(register_16_q), .in17(register_17_q),
    .in18(register_18_q), .in19(register_19_q), .in20(register_20_q), .in21(register_21_q),
    .in22(register_22_q), .in23(register_23_q), .in24(register_24_q), .in25(register_25_q),
    .in26(register_26_q), .in27(register_27_q), .in28(register_28_q), .in29(register_29_q),
    .in30(register_30_q), .in31(register_31_q), .out(X), .sel(XS));
  Decoder #(.enable("false"), .select(5)) decoder_2 (
    .out0(decoder_2_out0), .out1(decoder_2_out1), .out2(decoder_2_out2), .out3(decoder_2_out3),
    .out4(decoder_2_out4), .out5(decoder_2_out5), .out6(decoder_2_out6), .out7(decoder_2_out7),
    .out8(decoder_2_out8), .out9(decoder_2_out9), .out10(decoder_2_out10), .out11(decoder_2_out11),
    .out12(decoder_2_out12), .out13(decoder_2_out13), .out14(decoder_2_out14), .out15(decoder_2_out15),
    .out16(decoder_2_out16), .out17(decoder_2_out17), .out18(decoder_2_out18), .out19(decoder_2_out19),
    .out20(decoder_2_out20), .out21(decoder_2_out21), .out22(decoder_2_out22), .out23(decoder_2_out23),
    .out24(decoder_2_out24), .out25(decoder_2_out25), .out26(decoder_2_out26), .out27(decoder_2_out27),
    .out28(decoder_2_out28), .out29(decoder_2_out29), .out30(decoder_2_out30), .out31(decoder_2_out31),
    .sel(XS));
  LED led_33 (.in(decoder_2_out1));
  LED led_34 (.in(decoder_2_out3));
  LED led_35 (.in(decoder_2_out5));
  LED led_36 (.in(decoder_2_out0));
  LED led_37 (.in(decoder_2_out2));
  LED led_38 (.in(decoder_2_out4));
  LED led_39 (.in(decoder_2_out6));
  Multiplexer #(.select(5), .width(32)) multiplexer_2 (
    .in0({32{1'b0}}), .in1(register_1_q), .in2(register_2_q), .in3(register_3_q), .in4(register_4_q),
    .in5(register_5_q), .in6(register_6_q), .in7(register_7_q), .in8(register_8_q), .in9(register_9_q),
    .in10(register_10_q), .in11(register_11_q), .in12(register_12_q), .in13(register_13_q),
    .in14(register_14_q), .in15(register_15_q), .in16(register_16_q), .in17(register_17_q),
    .in18(register_18_q), .in19(register_19_q), .in20(register_20_q), .in21(register_21_q),
    .in22(register_22_q), .in23(register_23_q), .in24(register_24_q), .in25(register_25_q),
    .in26(register_26_q), .in27(register_27_q), .in28(register_28_q), .in29(register_29_q),
    .in30(register_30_q), .in31(register_31_q), .out(Y), .sel(YS));
  LED led_40 (.in(decoder_2_out7));
  LED led_41 (.in(decoder_2_out9));
  LED led_42 (.in(decoder_2_out11));
  LED led_43 (.in(decoder_2_out13));
  LED led_44 (.in(decoder_2_out8));
  LED led_45 (.in(decoder_2_out10));
  LED led_46 (.in(decoder_2_out12));
  LED led_47 (.in(decoder_2_out14));
  Decoder #(.enable("false"), .select(5)) decoder_3 (
    .out0(decoder_3_out0), .out1(decoder_3_out1), .out2(decoder_3_out2), .out3(decoder_3_out3),
    .out4(decoder_3_out4), .out5(decoder_3_out5), .out6(decoder_3_out6), .out7(decoder_3_out7),
    .out8(decoder_3_out8), .out9(decoder_3_out9), .out10(decoder_3_out10), .out11(decoder_3_out11),
    .out12(decoder_3_out12), .out13(decoder_3_out13), .out14(decoder_3_out14), .out15(decoder_3_out15),
    .out16(decoder_3_out16), .out17(decoder_3_out17), .out18(decoder_3_out18), .out19(decoder_3_out19),
    .out20(decoder_3_out20), .out21(decoder_3_out21), .out22(decoder_3_out22), .out23(decoder_3_out23),
    .out24(decoder_3_out24), .out25(decoder_3_out25), .out26(decoder_3_out26), .out27(decoder_3_out27),
    .out28(decoder_3_out28), .out29(decoder_3_out29), .out30(decoder_3_out30), .out31(decoder_3_out31),
    .sel(YS));
  LED led_48 (.in(decoder_3_out1));
  LED led_49 (.in(decoder_3_out3));
  LED led_50 (.in(decoder_3_out5));
  LED led_51 (.in(decoder_3_out7));
  LED led_52 (.in(decoder_3_out0));
  LED led_53 (.in(decoder_3_out2));
  LED led_54 (.in(decoder_3_out4));
  LED led_55 (.in(decoder_3_out6));
  LED led_56 (.in(decoder_2_out15));
  LED led_57 (.in(decoder_2_out17));
  LED led_58 (.in(decoder_2_out19));
  LED led_59 (.in(decoder_2_out21));
  LED led_60 (.in(decoder_2_out16));
  LED led_61 (.in(decoder_2_out18));
  LED led_62 (.in(decoder_2_out20));
  LED led_63 (.in(decoder_2_out22));
  LED led_64 (.in(decoder_3_out9));
  LED led_65 (.in(decoder_3_out11));
  LED led_66 (.in(decoder_3_out13));
  LED led_67 (.in(decoder_3_out15));
  LED led_68 (.in(decoder_3_out8));
  LED led_69 (.in(decoder_3_out10));
  LED led_70 (.in(decoder_3_out12));
  LED led_71 (.in(decoder_3_out14));
  LED led_72 (.in(decoder_2_out23));
  LED led_73 (.in(decoder_2_out25));
  LED led_74 (.in(decoder_2_out27));
  LED led_75 (.in(decoder_2_out29));
  LED led_76 (.in(decoder_2_out24));
  LED led_77 (.in(decoder_2_out26));
  LED led_78 (.in(decoder_2_out28));
  LED led_79 (.in(decoder_2_out30));
  LED led_80 (.in(decoder_3_out17));
  LED led_81 (.in(decoder_3_out19));
  LED led_82 (.in(decoder_3_out21));
  LED led_83 (.in(decoder_3_out23));
  LED led_84 (.in(decoder_3_out16));
  LED led_85 (.in(decoder_3_out18));
  LED led_86 (.in(decoder_3_out20));
  LED led_87 (.in(decoder_3_out22));
  LED led_88 (.in(decoder_2_out31));
  LED led_89 (.in(decoder_3_out25));
  LED led_90 (.in(decoder_3_out27));
  LED led_91 (.in(decoder_3_out29));
  LED led_92 (.in(decoder_3_out31));
  LED led_93 (.in(decoder_3_out24));
  LED led_94 (.in(decoder_3_out26));
  LED led_95 (.in(decoder_3_out28));
  LED led_96 (.in(decoder_3_out30));
endmodule

module plusfour (
  input  [31:0] A,
  output [31:0] V
);

  Adder #(.width(32)) adder_1 (.a(A), .b(32'h4), .out(V));  // open: cin, cout
endmodule

module northbridge (
  input  [31:0] Din,
  input  [31:0] DfromMem,
  input  [31:0] DfromIO,
  input  [31:0] A,
  input  write,
  input  read,
  input  clk,
  input  half,
  input  word,
  input  \signed ,
  output [31:0] Dout,
  output [31:0] DtoMem,
  output [11:0] AtoMem,
  output [31:0] DtoIO,
  output [11:0] AtoIO,
  output MemStr,
  output MemStr3,
  output MemStr2,
  output MemStr1,
  output MemStr0,
  output MemClk,
  output IORead,
  output IOWrite,
  output IOClk
);

  wire demultiplexer_2_out0, demultiplexer_2_out2, demultiplexer_3_out0, demultiplexer_3_out1,
       demultiplexer_3_out2, demultiplexer_3_out3, writebyte, writehalf, writeword;
  wire [7:0] multiplexer_2_out;
  wire [15:0] multiplexer_5_out;
  wire [31:0] bit_extender_1_out, bit_extender_2_out, bit_extender_3_out, bit_extender_4_out,
       multiplexer_3_out, multiplexer_4_out, multiplexer_7_out;

  Multiplexer #(.select(2), .width(32)) multiplexer_1 (
    .in0({Din[7:0], Din[7:0], Din[7:0], Din[7:0]}), .in1({Din[15:0], Din[15:0]}), .in2(Din), .out(DtoIO),
    .sel({word, half}));  // open: in3
  Demultiplexer #(.select(2)) demultiplexer_1 (
    .out0(writebyte), .out1(writehalf), .out2(writeword), .in(write), .sel({word, half}));  // open: out3
  Multiplexer #(.select(2), .width(8)) multiplexer_2 (
    .in0(DfromMem[31:24]), .in1(DfromMem[23:16]), .in2(DfromMem[15:8]), .in3(DfromMem[7:0]),
    .out(multiplexer_2_out), .sel(A[1:0]));
  and and_1 (IORead, A[31], read);
  and and_2 (IOWrite, A[31], write);
  Multiplexer #(.width(32)) multiplexer_3 (
    .in0(bit_extender_1_out), .in1(bit_extender_2_out), .out(multiplexer_3_out), .sel(\signed ));
  assign bit_extender_1_out = {{24{1'b0}}, multiplexer_2_out};  // Bit_Extender bit_extender_1
  assign bit_extender_2_out = {{24{multiplexer_2_out[7]}}, multiplexer_2_out};  // Bit_Extender bit_extender_2
  Multiplexer #(.select(2), .width(32)) multiplexer_4 (
    .in0(multiplexer_3_out), .in1(multiplexer_7_out), .in2(DfromMem), .out(multiplexer_4_out),
    .sel({word, half}));  // open: in3
  Multiplexer #(.select(2), .width(16)) multiplexer_5 (
    .in0(DfromMem[31:16]), .in2(DfromMem[15:0]), .out(multiplexer_5_out), .sel(A[1:0]));  // open: in1, in3
  Multiplexer #(.width(32)) multiplexer_6 (.in0(multiplexer_4_out), .in1(DfromIO), .out(Dout), .sel(A[31]));
  Multiplexer #(.width(32)) multiplexer_7 (
    .in0(bit_extender_3_out), .in1(bit_extender_4_out), .out(multiplexer_7_out), .sel(\signed ));
  assign bit_extender_3_out = {{16{1'b0}}, multiplexer_5_out};  // Bit_Extender bit_extender_3
  assign bit_extender_4_out = {{16{multiplexer_5_out[15]}}, multiplexer_5_out};  // Bit_Extender bit_extender_4
  Demultiplexer #(.select(2)) demultiplexer_2 (
    .out0(demultiplexer_2_out0), .out2(demultiplexer_2_out2), .in(writehalf), .sel(A[1:0]));  // open: out1, out3
  Demultiplexer #(.select(2)) demultiplexer_3 (
    .out0(demultiplexer_3_out0), .out1(demultiplexer_3_out1), .out2(demultiplexer_3_out2),
    .out3(demultiplexer_3_out3), .in(writebyte), .sel(A[1:0]));
  and and_3 (MemStr, write, ~A[31]);  // AND_Gate
  or or_1 (MemStr3, writeword, demultiplexer_2_out2, demultiplexer_3_out3);
  or or_2 (MemStr2, writeword, demultiplexer_2_out2, demultiplexer_3_out2);
  or or_3 (MemStr1, writeword, demultiplexer_2_out0, demultiplexer_3_out1);
  or or_4 (MemStr0, writeword, demultiplexer_2_out0, demultiplexer_3_out0);

  assign AtoIO = {A[11:2], 2'b00};
  assign AtoMem = {A[11:2], 2'b00};
  assign DtoMem = DtoIO;
  assign IOClk = clk;
  assign MemClk = clk;

  // Other names for the same wires on the sheet: HighAddr = A[31]; align[1:0] = A[1:0]; size[1:0] = {word, half}

  // Notes on the sheet:
  //   Big-endianWord in memory is AABBCCDDAddress 0 goes with high byte AAAddress 1 goes with next byte BBAddress 2 goes with next byte CCAddress 3 goes with low byte DD
  //   #size=0 means byte (1 byte) #size=1 means half (2 byte) #size=2 means word (4 byte)
  //   MIPS can support up to 4GB of memory(32 bit addresses, byte-addressed,so 2^32 possible addresses eachholding 1 byte).There is only 4KB of actual data memory(requiring 12 bit addresses). The northbridgeredirects all low-numbered addresses to this data memory.The northbridge redirects all accesses above 0x80000000 to the southbridge, where input/output devices are connected. The southbridge in turn redirects different addresses to different input/output devices. Summary of Address Mappings: 0x00000000 - start of data memory 0x00000FFF - end of data memory 0x80000000 - start of southbridge i/o range 0x80000000 - Keyboard status (read only, 1 bit) 0x80000004 - Keybaord data (read only, 8 bits) 0x80000008 - LCD data (write only, 8 bits) 0x8000000c - LED data (read/write, 10 bits) 0x80000010 - Button/Switch data (read only, 13 bits) 0xFFFFFFFFF - end of southbridge i/o range
  //   #0x00000000 - start of data memory
  //   0x00000FFF - end of data memory
  //   0x80000000 - Keyboard status (read only, 1 bit)
  //   0x80000004 - Keyboard data (read only, 8 bits)
  //   0x80000008 - Keyboard data (read only, 8 bits)
endmodule

module southbridge (
  input  [11:0] A,
  input  [31:0] Din,
  input  read,
  input  write,
  input  clk,
  input  [6:0] KbdData,
  input  KbdReady,
  input  [9:0] BtnData,
  input  [2:0] SwData,
  output [31:0] Dout,
  output [6:0] LcdData,
  output LcdWrite,
  output LcdClk,
  output KbdRead,
  output KbdClk,
  output [9:0] LedData,
  output [7:0] SevenData,
  output [31:0] UpperLedData,
  output [31:0] LowerLedData
);

  wire and_1_out, and_2_out, and_3_out, and_4_out, kbddata_t, kbdstatus, lcd, led, lowerled, seven, sw,
       upperled;
  wire [31:0] undriven;
  wire [31:8] SevenState_q;
  wire [31:10] LedState_q;

  Decoder #(.enable("false"), .select(3)) decoder_1 (
    .out0(kbdstatus), .out1(kbddata_t), .out2(lcd), .out3(led), .out4(sw), .out5(seven), .out6(upperled),
    .out7(lowerled), .sel(A[4:2]));
  Multiplexer #(.select(3), .width(32)) multiplexer_1 (
    .in0({{31{1'b0}}, KbdReady}), .in1({{25{1'b0}}, KbdData}), .in2(undriven), .in3({LedState_q, LedData}),
    .in4({{19{1'b0}}, SwData, BtnData}), .in5({SevenState_q, SevenData}), .in6(UpperLedData),
    .in7(LowerLedData), .out(Dout), .sel(A[4:2]));
  and and_1 (and_1_out, led, write);
  and and_2 (and_2_out, seven, write);
  and and_3 (and_3_out, upperled, write);
  and and_4 (and_4_out, lowerled, write);
  Register #(.width(32)) SevenState (.D(Din), .en(and_2_out), .Q({SevenState_q, SevenData}), .clk(clk));  // open: clr
  Register #(.width(32)) UpperLedState (.D(Din), .en(and_3_out), .Q(UpperLedData), .clk(clk));  // open: clr
  Register #(.width(32)) LowerLedState (.D(Din), .en(and_4_out), .Q(LowerLedData), .clk(clk));  // open: clr
  and and_5 (LcdWrite, lcd, write);
  and and_6 (KbdRead, kbddata_t, read);
  Register #(.width(32)) LedState (.D(Din), .en(and_1_out), .Q({LedState_q, LedData}), .clk(clk));  // open: clr

  assign KbdClk = clk;
  assign LcdClk = clk;
  assign LcdData = Din[6:0];
  // also tied to GND on the sheet: {SevenState_q[8], SevenState_q[9], SevenState_q[10], SevenState_q[11], SevenState_q[12], SevenState_q[13], SevenState_q[14], SevenState_q[15], SevenState_q[16], SevenState_q[17], SevenState_q[18], SevenState_q[19], SevenState_q[20], SevenState_q[21], SevenState_q[22], SevenState_q[23], SevenState_q[24], SevenState_q[25], SevenState_q[26], SevenState_q[27], SevenState_q[28], SevenState_q[29], SevenState_q[30], SevenState_q[31]}

  // Notes on the sheet:
  //   (to northbridge)
  //   (from northbridge)
endmodule

module plus (
  input  [31:0] A,
  input  [31:0] B,
  output [31:0] V
);

  Adder #(.width(32)) adder_1 (.a(A), .b(B), .out(V));  // open: cin, cout
endmodule
